# Fritzing sketch restaurantPager (saved by Fritzing 0.9.3b)
breadboards: 1

parts:
  Part1 = Arduino Uno (Rev3)
  7_Segment1 = 7 Segment Display
  J1 = Piezo Speaker
  S1 = Pushbutton [package="[THT]"]
  R1 = Resistor [tolerance=±5% resistance=220 package=THT]

nets (from the schematic view):
  N1: Part1.D8, 7_Segment1.Segment_C
  N2: Part1.D9_PWM, 7_Segment1.Segment_D
  N3: Part1.D10_PWM/SS, 7_Segment1.Segment_E
  N4: Part1.D11_PWM/MOSI, S1.Pin_1, S1.Pin_2, R1.Pin_0
  N5: Part1.D2, J1.pin1
  N6: Part1.D3_PWM, 7_Segment1.Segment_B
  N7: Part1.D4, 7_Segment1.Segment_A#10
  N8: Part1.D5_PWM, 7_Segment1.Segment_F
  N9: Part1.D6_PWM, 7_Segment1.Segment_A#1
  N10: Part1.D7, 7_Segment1.Segment_DP
  N11: Part1.5V, 7_Segment1.common_cathode#8, J1.pin2, R1.Pin_1
  N12: Part1.GND, S1.Pin_3, S1.Pin_4

// code stored in the sketch: alet.ino
const int buzzerPin = 2;
const int segmentG = 6;
const int segmentF = 5;
const int segmentE = 10;
const int segmentD = 9;
const int segmentPoint = 7;
const int segmentC = 8;
const int segmentB = 3;
const int segmentA = 4;
const int button = 11;
int numberGlobal = 0;
int repeatNumber = 0;
bool isClick = false;
unsigned long previousMillis = 0;
const long interval = 1000; // 1 saniye
long counter = 0;


void writeNumber(uint8_t g, uint8_t f, uint8_t e, uint8_t d, uint8_t c, uint8_t b, uint8_t a, int number)
{
  digitalWrite(segmentG,g);
  digitalWrite(segmentF,f);
  digitalWrite(segmentE,e);
  digitalWrite(segmentD,d);
  digitalWrite(segmentC,c);
  digitalWrite(segmentB,b);
  digitalWrite(segmentA,a);
  digitalWrite(segmentPoint, HIGH);
}


void displayNumber(int number)
{
  if(number == 0)
  {
    writeNumber(HIGH, LOW, LOW, LOW, LOW, LOW, LOW, 0);
  }


  if(number == 1)
  {
    writeNumber(HIGH, HIGH, HIGH, HIGH, LOW, LOW, HIGH, 1);
  }


  else if(number == 2)
  {
    writeNumber(LOW, HIGH, LOW, LOW, HIGH, LOW, LOW, 2);
  }


  else if(number == 3)
  {
    writeNumber(LOW, HIGH, HIGH, LOW, LOW, LOW, LOW, 3);
  }


  if(number == 4)
  {
    writeNumber(LOW, LOW, HIGH, HIGH, LOW, LOW, HIGH, 4);
  }


  if(number == 5)
  {
    writeNumber(LOW, LOW, HIGH, LOW, LOW, HIGH, LOW, 5);
  }


  else if(number == 6)
  {
    writeNumber(LOW, LOW, LOW, LOW, LOW, HIGH, LOW, 6);
  }


  else if(number == 7)
  {
    writeNumber(HIGH, HIGH, HIGH, HIGH, LOW, LOW, LOW, 7);
  }


  else if(number == 8)
  {
    writeNumber(LOW, LOW, LOW, LOW, LOW, LOW, LOW, 8);
  }


  else if(number == 9)
  {
    writeNumber(LOW, LOW, HIGH, LOW, LOW, LOW, LOW, 9);
  }
}


void control()
{
  if(digitalRead(button) == 1)
  {
    repeatNumber++;
    
    if(repeatNumber == 1)
    {
      isClick = !isClick;


      if(!isClick)
      {
        numberGlobal = random(9);
      }
    }
  }


  else 
  {
    repeatNumber = 0;
  }
}


void setup()
{
  randomSeed(analogRead(0));
  Serial.begin(9600);


  pinMode(buzzerPin, OUTPUT);
  pinMode(segmentG, OUTPUT);
  pinMode(segmentF, OUTPUT);
  pinMode(segmentE, OUTPUT);
  pinMode(segmentD, OUTPUT);
  pinMode(segmentPoint, OUTPUT);
  pinMode(segmentC, OUTPUT);
  pinMode(segmentB, OUTPUT);
  pinMode(segmentA, OUTPUT);
  pinMode(button, INPUT);


  numberGlobal = random(9);
}


void loop()
{
  unsigned long currentMillis = millis();
  control();


  if(isClick)
  {
    if (currentMillis - previousMillis >= interval) {
        // Her 1 saniyede bir yap?lacak i?lemler
        counter++;
        if(counter % 2 == 0)
        {
          noTone(buzzerPin);
          writeNumber(HIGH, HIGH, HIGH, HIGH, HIGH, HIGH, HIGH, numberGlobal);
        }


        else
        {
          tone(buzzerPin, 1000);
          displayNumber(numberGlobal);
        }
        
        // Zaman damgas?n? güncelle
        previousMillis = currentMillis;
    }


    control();
  }


  else
  {
    displayNumber(numberGlobal);
    noTone(buzzerPin);
  }



}
